// Logisim project Contador.circ as structural Verilog: 1 circuit, main circuit main
module main (
  input  Clear,
  input  [7:0] in_2,
  input  Enable,
  input  Reloj,
  input  [7:0] in_5,
  input  [7:0] in_6,
  output [7:0] out_7
);

  wire comparator_2_eq, or_1_out;

  or or_1 (or_1_out, Clear, comparator_2_eq);
  Counter counter_1 (.load(or_1_out), .up(1'b1), .count(Enable), .clk(Reloj), .D(in_5), .Q(out_7));  // open: clr, carry
  Comparator comparator_1 (.a(in_2), .b(out_7));  // open: gt, eq, lt
  Comparator comparator_2 (.a(out_7), .b(in_6), .eq(comparator_2_eq));  // open: gt, lt

  // Notes on the sheet:
  //   El "Clear" reseteara a 48, NO 0
  //   Si fuera 55, reseteamos en el proximo tick
  //   if 52 == salida del contador then sumar 52 + 3 (a completar :))
endmodule
