// Logisim project FuncionesF1F2.circ as structural Verilog: 3 circuits, main circuit Funciones
module Funciones (
  input  Z4,
  input  Z3,
  input  Z2,
  input  Z1,
  input  A,
  input  B,
  input  C,
  input  D,
  input  E,
  output F1ANDF2
);

  wire func_f1_1_f1, func_f2_1_f2;

  func_F1 func_f1_1 (.Z4(Z4), .Z3(Z3), .Z2(Z2), .Z1(Z1), .F1(func_f1_1_f1));
  func_F2 func_f2_1 (.A(A), .B(B), .C(C), .D(D), .E(E), .F2(func_f2_1_f2));
  and and_1 (F1ANDF2, func_f1_1_f1, func_f2_1_f2);
endmodule

module func_F1 (
  input  Z4,
  input  Z3,
  input  Z2,
  input  Z1,
  output F1
);

  ROM #(.addrWidth(4), .dataWidth(1)) rom_1 (.addr({Z1, Z2, Z3, Z4}));  // open: data

  // Notes on the sheet:
  //   contents of rom_1 (hex, n*v repeats v):
  //   1 4*0 1 0 0 1 1 0 1 1 0 1 1
endmodule

module func_F2 (
  input  A,
  input  B,
  input  C,
  input  D,
  input  E,
  output F2
);

  wire and_1_out, and_2_out, and_3_out, and_4_out, and_5_out, and_6_out, and_7_out, and_8_out, and_9_out,
       not_1_out, not_2_out, not_3_out, not_4_out, not_5_out;

  not not_1 (not_1_out, A);
  not not_2 (not_2_out, B);
  not not_3 (not_3_out, C);
  not not_4 (not_4_out, D);
  not not_5 (not_5_out, E);
  and and_1 (and_1_out, not_2_out, D, not_5_out);
  and and_2 (and_2_out, not_1_out, B, not_3_out, E);
  and and_3 (and_3_out, B, C, not_4_out, not_5_out);
  and and_4 (and_4_out, not_2_out, not_4_out, E);
  and and_5 (and_5_out, A, B, C, D, E);
  and and_6 (and_6_out, A, B, not_3_out, not_4_out);
  and and_7 (and_7_out, A, B, not_3_out, not_5_out);
  and and_8 (and_8_out, A, not_2_out, not_3_out, E);
  and and_9 (and_9_out, not_1_out, not_2_out, C, E);
  or or_1 (F2, and_1_out, and_2_out, and_3_out, and_4_out, and_5_out, and_6_out, and_7_out, and_8_out, and_9_out);
endmodule
